// Logisim project PongV2.circ as structural Verilog: 2 circuits, main circuit main
module main (
);

  wire and_1_out, and_2_out, and_4_out, cdm_8_1_p2, cdm_8_1_p4, cdm_8_1_p5, cdm_8_1_p6, cdm_8_1_p7,
       cdm_8_1_p8, cdm_8_1_p9, cdm_8_1_p10, Clk, decoder_1_out1, decoder_1_out2, decoder_1_out3,
       decoder_1_out4, decoder_1_out5, F8, FE___Ball_X, FF_Ball_Y, I_O_Sel, not_1_out, not_2_out, not_3_out,
       not_4_out, or_1_out, Rd_Wr, Reset;
  wire [2:0] I_O_Adr;
  wire [6:0] keyboard_1_data;
  wire [7:0] cdm_8_1_p13, cdm_8_1_p14, controlled_buffer_7_out, I_O_Dat, Keyboard, register_1_q,
       shifter_1_out;
  wire [7:3] cdm_8_1_p12;
  wire [31:0] multiplexer_1_out, multiplexer_2_out, multiplexer_3_out, multiplexer_4_out, multiplexer_5_out,
       multiplexer_6_out, multiplexer_7_out, multiplexer_8_out, multiplexer_9_out, multiplexer_10_out,
       multiplexer_11_out, multiplexer_12_out, multiplexer_13_out, multiplexer_14_out, multiplexer_15_out,
       multiplexer_16_out, multiplexer_17_out, multiplexer_18_out, multiplexer_19_out, multiplexer_20_out,
       multiplexer_21_out, multiplexer_22_out, multiplexer_23_out, multiplexer_24_out, multiplexer_25_out,
       multiplexer_26_out, multiplexer_27_out, multiplexer_28_out, multiplexer_29_out, multiplexer_30_out,
       multiplexer_31_out, multiplexer_32_out, undriven, undriven_2;

  Keyboard keyboard_1 (.clk(Clk), .data(keyboard_1_data));  // open: re, clr, avail
  Multiplexer #(.width(32), .enable("false")) multiplexer_1 (
    .in0({32{1'b0}}), .in1(undriven), .out(multiplexer_1_out), .sel(undriven_2[31]));
  Multiplexer #(.width(32), .enable("false")) multiplexer_2 (
    .in0({32{1'b0}}), .in1(undriven), .out(multiplexer_2_out), .sel(undriven_2[30]));
  not not_1 (not_1_out, or_1_out);
  or or_1 (or_1_out, and_1_out, and_2_out);
  Multiplexer #(.width(32), .enable("false")) multiplexer_3 (
    .in0({32{1'b0}}), .in1(undriven), .out(multiplexer_3_out), .sel(undriven_2[29]));
  Multiplexer #(.width(32), .enable("false")) multiplexer_4 (
    .in0({32{1'b0}}), .in1(undriven), .out(multiplexer_4_out), .sel(undriven_2[28]));
  assign Keyboard = not_1_out ? {8{1'b0}} : 8'bz;  // Controlled_Buffer controlled_buffer_1
  and and_1 (and_1_out, keyboard_1_data[6], keyboard_1_data[5], keyboard_1_data[4], ~keyboard_1_data[3], keyboard_1_data[2], keyboard_1_data[1], keyboard_1_data[0]);  // AND_Gate
  and and_2 (and_2_out, keyboard_1_data[6], keyboard_1_data[5], keyboard_1_data[4], ~keyboard_1_data[3], ~keyboard_1_data[2], keyboard_1_data[1], keyboard_1_data[0]);  // AND_Gate
  Multiplexer #(.width(32), .enable("false")) multiplexer_5 (
    .in0({32{1'b0}}), .in1(undriven), .out(multiplexer_5_out), .sel(undriven_2[27]));
  // Probe on Keyboard
  assign Keyboard = and_1_out ? 8'h1 : 8'bz;  // Controlled_Buffer controlled_buffer_2
  assign Keyboard = and_2_out ? 8'h2 : 8'bz;  // Controlled_Buffer controlled_buffer_3
  Multiplexer #(.width(32), .enable("false")) multiplexer_6 (
    .in0({32{1'b0}}), .in1(undriven), .out(multiplexer_6_out), .sel(undriven_2[25]));
  Multiplexer #(.width(32), .enable("false")) multiplexer_7 (
    .in0({32{1'b0}}), .in1(undriven), .out(multiplexer_7_out), .sel(undriven_2[26]));
  Multiplexer #(.width(32), .enable("false")) multiplexer_8 (
    .in0({32{1'b0}}), .in1(undriven), .out(multiplexer_8_out), .sel(undriven_2[24]));
  assign I_O_Dat = F8 ? Keyboard : 8'bz;  // Controlled_Buffer controlled_buffer_4
  Multiplexer #(.width(32), .enable("false")) multiplexer_9 (
    .in0({32{1'b0}}), .in1(undriven), .out(multiplexer_9_out), .sel(undriven_2[23]));
  Multiplexer #(.width(32), .enable("false")) multiplexer_10 (
    .in0({32{1'b0}}), .in1(undriven), .out(multiplexer_10_out), .sel(undriven_2[22]));
  Multiplexer #(.width(32), .enable("false")) multiplexer_11 (
    .in0({32{1'b0}}), .in1(undriven), .out(multiplexer_11_out), .sel(undriven_2[21]));
  Multiplexer #(.width(32), .enable("false")) multiplexer_12 (
    .in0({32{1'b0}}), .in1(undriven), .out(multiplexer_12_out), .sel(undriven_2[20]));
  DotMatrix #(.matrixcols(32), .matrixrows(32)) dotmatrix_1 (
    .col0(multiplexer_1_out), .col1(multiplexer_2_out), .col2(multiplexer_3_out), .col3(multiplexer_4_out),
    .col4(multiplexer_5_out), .col5(multiplexer_7_out), .col6(multiplexer_6_out), .col7(multiplexer_8_out),
    .col8(multiplexer_9_out), .col9(multiplexer_10_out), .col10(multiplexer_11_out),
    .col11(multiplexer_12_out), .col12(multiplexer_13_out), .col13(multiplexer_15_out),
    .col14(multiplexer_14_out), .col15(multiplexer_16_out), .col16(multiplexer_18_out),
    .col17(multiplexer_17_out), .col18(multiplexer_20_out), .col19(multiplexer_19_out),
    .col20(multiplexer_21_out), .col21(multiplexer_23_out), .col22(multiplexer_22_out),
    .col23(multiplexer_24_out), .col24(multiplexer_25_out), .col25(multiplexer_26_out),
    .col26(multiplexer_28_out), .col27(multiplexer_27_out), .col28(multiplexer_29_out),
    .col29(multiplexer_31_out), .col30(multiplexer_30_out), .col31(multiplexer_32_out));
  Multiplexer #(.width(32), .enable("false")) multiplexer_13 (
    .in0({32{1'b0}}), .in1(undriven), .out(multiplexer_13_out), .sel(undriven_2[19]));
  Multiplexer #(.width(32), .enable("false")) multiplexer_14 (
    .in0({32{1'b0}}), .in1(undriven), .out(multiplexer_14_out), .sel(undriven_2[17]));
  Multiplexer #(.width(32), .enable("false")) multiplexer_15 (
    .in0({32{1'b0}}), .in1(undriven), .out(multiplexer_15_out), .sel(undriven_2[18]));
  Multiplexer #(.width(32), .enable("false")) multiplexer_16 (
    .in0({32{1'b0}}), .in1(undriven), .out(multiplexer_16_out), .sel(undriven_2[16]));
  Multiplexer #(.width(32), .enable("false")) multiplexer_17 (
    .in0({32{1'b0}}), .in1(undriven), .out(multiplexer_17_out), .sel(undriven_2[14]));
  Multiplexer #(.width(32), .enable("false")) multiplexer_18 (
    .in0({32{1'b0}}), .in1(undriven), .out(multiplexer_18_out), .sel(undriven_2[15]));
  Multiplexer #(.width(32), .enable("false")) multiplexer_19 (
    .in0({32{1'b0}}), .in1(undriven), .out(multiplexer_19_out), .sel(undriven_2[12]));
  Multiplexer #(.width(32), .enable("false")) multiplexer_20 (
    .in0({32{1'b0}}), .in1(undriven), .out(multiplexer_20_out), .sel(undriven_2[13]));
  // Probe on cdm_8_1_p4
  // Probe on cdm_8_1_p2
  Clock clock_1 (.out(Clk));
  Button button_1 (.out(Reset));
  Multiplexer #(.width(32), .enable("false")) multiplexer_21 (
    .in0({32{1'b0}}), .in1(undriven), .out(multiplexer_21_out), .sel(undriven_2[11]));
  // Probe on cdm_8_1_p5
  // Probe on cdm_8_1_p6
  // Probe on cdm_8_1_p7
  Multiplexer #(.width(32), .enable("false")) multiplexer_22 (
    .in0({32{1'b0}}), .in1(undriven), .out(multiplexer_22_out), .sel(undriven_2[9]));
  Multiplexer #(.width(32), .enable("false")) multiplexer_23 (
    .in0({32{1'b0}}), .in1(undriven), .out(multiplexer_23_out), .sel(undriven_2[10]));
  // Probe on cdm_8_1_p9
  // Probe on cdm_8_1_p8
  Multiplexer #(.width(32), .enable("false")) multiplexer_24 (
    .in0({32{1'b0}}), .in1(undriven), .out(multiplexer_24_out), .sel(undriven_2[8]));
  not not_2 (not_2_out, Rd_Wr);
  assign I_O_Dat = not_2_out ? cdm_8_1_p13 : 8'bz;  // Controlled_Buffer controlled_buffer_5
  // CdM_8 cdm_8_1: pin names not known; wires that end beside it: Clk, cdm_8_1_p2, Reset, cdm_8_1_p4, cdm_8_1_p5, cdm_8_1_p6, cdm_8_1_p7, cdm_8_1_p8, cdm_8_1_p9, cdm_8_1_p10, Rd_Wr, {cdm_8_1_p12, I_O_Adr}, cdm_8_1_p13, cdm_8_1_p14
  assign cdm_8_1_p14 = Rd_Wr ? I_O_Dat : 8'bz;  // Controlled_Buffer controlled_buffer_6
  not not_3 (not_3_out, I_O_Sel);
  Multiplexer #(.width(32), .enable("false")) multiplexer_25 (
    .in0({32{1'b0}}), .in1(undriven), .out(multiplexer_25_out), .sel(undriven_2[7]));
  Multiplexer #(.width(32), .enable("false")) multiplexer_26 (
    .in0({32{1'b0}}), .in1(undriven), .out(multiplexer_26_out), .sel(undriven_2[6]));
  and and_3 (I_O_Sel, cdm_8_1_p10, cdm_8_1_p12[7], cdm_8_1_p12[6], cdm_8_1_p12[5], cdm_8_1_p12[4], cdm_8_1_p12[3]);
  Multiplexer #(.width(32), .enable("false")) multiplexer_27 (
    .in0({32{1'b0}}), .in1(undriven), .out(multiplexer_27_out), .sel(undriven_2[4]));
  Multiplexer #(.width(32), .enable("false")) multiplexer_28 (
    .in0({32{1'b0}}), .in1(undriven), .out(multiplexer_28_out), .sel(undriven_2[5]));
  // Probe on {cdm_8_1_p12, I_O_Adr}
  and and_4 (and_4_out, cdm_8_1_p10, not_3_out);
  Multiplexer #(.width(32), .enable("false")) multiplexer_29 (
    .in0({32{1'b0}}), .in1(undriven), .out(multiplexer_29_out), .sel(undriven_2[3]));
  RAM ram_1 (.addr({cdm_8_1_p12, I_O_Adr}), .data(I_O_Dat), .sel(and_4_out), .clk(Clk), .ld(Rd_Wr));  // open: clr
  Multiplexer #(.width(32), .enable("false")) multiplexer_30 (
    .in0({32{1'b0}}), .in1(undriven), .out(multiplexer_30_out), .sel(undriven_2[1]));
  Multiplexer #(.width(32), .enable("false")) multiplexer_31 (
    .in0({32{1'b0}}), .in1(undriven), .out(multiplexer_31_out), .sel(undriven_2[2]));
  // Probe on I_O_Dat
  Decoder #(.select(3), .disabled(0)) decoder_1 (
    .out0(F8), .out1(decoder_1_out1), .out2(decoder_1_out2), .out3(decoder_1_out3), .out4(decoder_1_out4),
    .out5(decoder_1_out5), .out6(FE___Ball_X), .out7(FF_Ball_Y), .sel(I_O_Adr), .en(I_O_Sel));
  Multiplexer #(.width(32), .enable("false")) multiplexer_32 (
    .in0({32{1'b0}}), .in1(undriven), .out(multiplexer_32_out), .sel(undriven_2[0]));
  // Probe on I_O_Adr
  LED led_1 (.in(F8));
  LED led_2 (.in(decoder_1_out1));
  not not_4 (not_4_out, FE___Ball_X);
  LED led_3 (.in(decoder_1_out2));
  LED led_4 (.in(decoder_1_out3));
  LED led_5 (.in(decoder_1_out4));
  LED led_6 (.in(decoder_1_out5));
  assign controlled_buffer_7_out = not_4_out ? register_1_q : 8'bz;  // Controlled_Buffer controlled_buffer_7
  assign controlled_buffer_7_out = FE___Ball_X ? I_O_Dat : 8'bz;  // Controlled_Buffer controlled_buffer_8
  Register register_1 (.D(controlled_buffer_7_out), .en(FE___Ball_X), .Q(register_1_q), .clk(Clk));  // open: clr
  LED led_7 (.in(FE___Ball_X));
  // Probe on register_1_q
  LED led_8 (.in(FF_Ball_Y));
  // Probe on shifter_1_out
  Shifter #(.shift("ar")) shifter_1 (.in(register_1_q), .\dist (3'b011), .out(shifter_1_out));

  // Notes on the sheet:
  //   Keyboard Input-W,S,x
endmodule

module CDM8 (
);

  wire and_2_out, cdm_8_1_p2, cdm_8_1_p4, cdm_8_1_p5, cdm_8_1_p6, cdm_8_1_p7, cdm_8_1_p8, cdm_8_1_p9,
       cdm_8_1_p10, Clk, decoder_1_out0, decoder_1_out1, decoder_1_out2, decoder_1_out3, decoder_1_out4,
       decoder_1_out5, decoder_1_out6, decoder_1_out7, I_O_Sel, not_1_out, not_2_out, Rd_Wr, Reset;
  wire [2:0] I_O_Adr;
  wire [7:0] cdm_8_1_p13, cdm_8_1_p14, I_O_Dat;
  wire [7:3] cdm_8_1_p12;

  // Probe on cdm_8_1_p2
  Button button_1 (.out(Reset));
  Clock clock_1 (.out(Clk));
  Decoder #(.select(3)) decoder_1 (
    .out0(decoder_1_out0), .out1(decoder_1_out1), .out2(decoder_1_out2), .out3(decoder_1_out3),
    .out4(decoder_1_out4), .out5(decoder_1_out5), .out6(decoder_1_out6), .out7(decoder_1_out7),
    .sel(I_O_Adr), .en(I_O_Sel));
  // Probe on cdm_8_1_p4
  // Probe on cdm_8_1_p6
  // Probe on cdm_8_1_p5
  Keyboard keyboard_1 ();  // open: clk, re, clr, avail, data
  LED led_1 (.in(decoder_1_out0));
  LED led_2 (.in(decoder_1_out1));
  LED led_3 (.in(decoder_1_out2));
  LED led_4 (.in(decoder_1_out3));
  // Probe on cdm_8_1_p8
  // Probe on cdm_8_1_p7
  LED led_5 (.in(decoder_1_out4));
  LED led_6 (.in(decoder_1_out5));
  LED led_7 (.in(decoder_1_out6));
  LED led_8 (.in(decoder_1_out7));
  // Probe on cdm_8_1_p9
  not not_1 (not_1_out, Rd_Wr);
  // CdM_8 cdm_8_1: pin names not known; wires that end beside it: Clk, cdm_8_1_p2, Reset, cdm_8_1_p4, cdm_8_1_p5, cdm_8_1_p6, cdm_8_1_p7, cdm_8_1_p8, cdm_8_1_p9, cdm_8_1_p10, Rd_Wr, {cdm_8_1_p12, I_O_Adr}, cdm_8_1_p13, cdm_8_1_p14, Rd_Wr
  assign I_O_Dat = not_1_out ? cdm_8_1_p13 : 8'bz;  // Controlled_Buffer controlled_buffer_1
  assign cdm_8_1_p14 = Rd_Wr ? I_O_Dat : 8'bz;  // Controlled_Buffer controlled_buffer_2
  not not_2 (not_2_out, I_O_Sel);
  and and_1 (I_O_Sel, cdm_8_1_p10, cdm_8_1_p12[7], cdm_8_1_p12[6], cdm_8_1_p12[5], cdm_8_1_p12[4], cdm_8_1_p12[3]);
  // Probe on {cdm_8_1_p12, I_O_Adr}
  and and_2 (and_2_out, cdm_8_1_p10, not_2_out);
  // Probe on I_O_Dat
  RAM ram_1 (.addr({cdm_8_1_p12, I_O_Adr}), .data(I_O_Dat), .sel(and_2_out), .clk(Clk), .ld(Rd_Wr));  // open: clr
endmodule
